# Fritzing sketch Wiring (saved by Fritzing 0.9.3b)
breadboards: 1

parts:
  Teensy1 = Teensy 3.6 (Basic)
  Bauteil1 = OLED 1.5" 128x128 [part_number=13392]

nets:
  GND: Teensy1.GND, Teensy1.GND1, Bauteil1.GND
  N1: Teensy1.D6, Bauteil1.RESET
  N2: Teensy1.D7, Bauteil1.DC
  N3: Teensy1.D10, Bauteil1.CS
  N4: Teensy1.D11, Bauteil1.MOSI
  N5: Teensy1.D13, Bauteil1.SCK
  3V3: Teensy1.3V3, Teensy1.3V3_1, Bauteil1.VCC

custom parts:
  Teensy 3.6 (Basic): The Teensy is a complete USB-based microcontoller development system, in a very small footprint, capable of implementing many types of projects. All programming is done via the USB port. No special programmer is needed, only a standard micro-USB cable and a PC or Macintosh with a USB port.
